// Logisim project Digital_Clock.circ as structural Verilog: 3 circuits, main circuit main
// State register
module main (
);

  wire B1_Deb, B1_out, B2_Deb, B2_out, CK, RST_out;
  wire [1:0] fsm_logic_1_s0_0, State_register_q;

  Button B1 (.out(B1_out));
  Button B2 (.out(B2_out));
  Clock u_CK (.out(CK));
  Debouncer u_B1_Deb (.CK(CK), .Button_input(B1_out), .O(B1_Deb));  // open: O_INV
  Debouncer u_B2_Deb (.CK(CK), .Button_input(B2_out), .O(B2_Deb));  // open: O_INV
  FSM_Logic fsm_logic_1 (
    .S1(State_register_q[1]), .S0(State_register_q[0]), .B1(B1_Deb), .S1_o(fsm_logic_1_s0_0[1]),
    .S0_0(fsm_logic_1_s0_0[0]));
  Button RST (.out(RST_out));
  Register #(.width(2)) State_register (.D(fsm_logic_1_s0_0), .en(1'b1), .clk(CK), .Q(State_register_q), .clr(RST_out));
endmodule

module FSM_Logic (
  input  S1,
  input  S0,
  input  B1,
  output S1_o,
  output S0_0
);

  wire and_1_out, and_2_out, not_1_out, not_2_out, not_3_out, xor_1_out, xor_2_out, xor_3_out, xor_4_out;

  not not_1 (not_1_out, B1);
  xor xor_1 (xor_1_out, S1, S0);
  not not_2 (not_2_out, S1);
  not not_3 (not_3_out, S0);
  and and_1 (and_1_out, S1, not_1_out);
  and and_2 (and_2_out, xor_1_out, B1);
  xor xor_2 (xor_2_out, B1, not_2_out);
  xor xor_3 (xor_3_out, B1, S0);
  xor xor_4 (xor_4_out, S1, not_3_out);
  or S1_nxt (S1_o, and_1_out, and_2_out);
  or S0_nxt (S0_0, xor_2_out, xor_3_out, xor_4_out);
endmodule

module Debouncer (
  input  CK,
  input  Button_input,
  output O,
  output O_INV
);

  wire and_1_out, and_2_out, d_ff_1_q, d_ff_1_qn, d_ff_2_q, d_ff_2_qn, d_ff_3_q, d_ff_3_qn, not_1_out;

  and and_1 (and_1_out, CK, Button_input);
  D_Flip_Flop d_ff_1 (.D(d_ff_1_qn), .clk(and_1_out), .Q(d_ff_1_q), .Qn(d_ff_1_qn), .reset(not_1_out));  // open: preset
  not not_1 (not_1_out, Button_input);
  D_Flip_Flop d_ff_2 (.D(d_ff_2_qn), .clk(d_ff_1_qn), .Q(d_ff_2_q), .Qn(d_ff_2_qn), .reset(not_1_out));  // open: preset
  D_Flip_Flop d_ff_3 (.D(d_ff_3_qn), .clk(d_ff_2_qn), .Q(d_ff_3_q), .Qn(d_ff_3_qn), .reset(not_1_out));  // open: preset
  and and_2 (and_2_out, d_ff_1_q, d_ff_2_q, d_ff_3_q);
  D_Flip_Flop d_ff_4 (.D(and_2_out), .clk(CK), .Q(O), .Qn(O_INV));  // open: preset, reset
endmodule
